# Fritzing sketch arduino_button-nopullup (saved by Fritzing 0.8.3b)
breadboards: 1

parts:
  Part1 = Arduino Uno (Rev3)
  S1 = Pushbutton [package="[THT]"]

nets:
  N1: Part1.GND, S1.Pin_1, S1.Pin_2
  N2: Part1.D7, Part1.5V, S1.Pin_3, S1.Pin_4
