# Fritzing sketch arduino_button-pullup (saved by Fritzing 0.8.3b)
breadboards: 1

parts:
  Part1 = Arduino Uno (Rev3)
  R1 = Resistor [tolerance=±5% resistance=1M package=THT]
  J1 = Piezo Speaker

nets:
  N1: Part1.A0, R1.Pin_1, J1.pin1
  N2: Part1.GND, R1.Pin_0, J1.pin2
