# Fritzing sketch arduino_pot (saved by Fritzing 0.8.3b)
breadboards: 1

parts:
  R1 = Rotary Potentiometer (Small)
  Part1 = Arduino Uno (Rev3)

nets:
  N1: R1.leg1, Part1.GND
  N2: R1.wiper, Part1.A0
  N3: R1.leg2, Part1.5V
